// Logisim project ULA.circ as structural Verilog: 1 circuit, main circuit main
module main (
  input  [31:0] A,
  input  [31:0] B,
  input  [4:0] shamt,
  input  [3:0] op,
  output zero,
  output [31:0] S,
  output overflow
);

  // AND_Gate and_1 is placed but not wired
  // OR_Gate or_1 is placed but not wired
  // NOR_Gate nor_1 is placed but not wired
  // XOR_Gate xor_1 is placed but not wired
  Adder #(.width(32)) adder_1 ();  // open: a, b, out, cin, cout
  Subtractor #(.width(32)) subtractor_1 ();  // open: a, b, out, bin, bout
  Shifter #(.width(32)) shifter_1 (.\dist (shamt));  // open: in, out
  Shifter #(.width(32), .shift("lr")) shifter_2 (.\dist (shamt));  // open: in, out
  Multiplexer #(.select(4), .width(32), .enable("false")) multiplexer_1 (
    .out(S), .sel(op));  // open: in0, in1, in2, in3, in4, in5, in6, in7, in8, in9, in10, in11, in12, in13, in14, in15
endmodule
